// Logisim project computer.circ as structural Verilog
module main (
  input  [7:0] in_1,
  input  [7:0] in_2,
  output [8:0] out_3
);

  Add_8 add_8_1 (
    .A0(in_1[0]), .A1(in_1[1]), .A2(in_1[2]), .A3(in_1[3]), .A4(in_1[4]), .A5(in_1[5]), .A6(in_1[6]),
    .AN(in_1[7]), .B0(in_2[0]), .B1(in_2[1]), .B2(in_2[2]), .B3(in_2[3]), .B4(in_2[4]), .B5(in_2[5]),
    .B6(in_2[6]), .BN(in_2[7]), .S0(out_3[0]), .S1(out_3[1]), .S2(out_3[2]), .S3(out_3[3]), .S4(out_3[4]),
    .S5(out_3[5]), .S6(out_3[6]), .SN(out_3[7]), .SO(out_3[8]));
endmodule

module semiadder (
  input  A,
  input  B,
  output U,
  output S
);

  and and_1 (U, A, B);
  xor xor_1 (S, A, B);
endmodule

module fulladder (
  input  A,
  input  B,
  input  D,
  output U,
  output S
);

  wire semiadder_1_s, semiadder_1_u, semiadder_2_u;

  semiadder semiadder_1 (.A(A), .B(B), .U(semiadder_1_u), .S(semiadder_1_s));
  semiadder semiadder_2 (.A(semiadder_1_s), .B(D), .U(semiadder_2_u), .S(S));
  or or_1 (U, semiadder_1_u, semiadder_2_u);
endmodule

module D_Flip_Flop (
  input  S,
  input  D,
  input  E,
  input  R,
  output out_5,
  output out_6
);

  wire and_1_out, and_2_out, and_3_out, and_4_out, nor_1_out, nor_2_out, nor_3_out;

  and and_1 (and_1_out, D, E);
  and and_2 (and_2_out, ~D, E);  // AND_Gate
  nor nor_1 (nor_1_out, S, R);
  and and_3 (and_3_out, and_1_out, nor_1_out);
  and and_4 (and_4_out, nor_1_out, and_2_out);
  nor nor_2 (nor_2_out, S, and_3_out);
  nor nor_3 (nor_3_out, and_4_out, R);
  nand nand_1 (out_5, nor_2_out, out_6);
  nand nand_2 (out_6, out_5, nor_3_out);
endmodule

module Sel_2 (
  input  _0,
  input  _1,
  input  S,
  output U
);

  wire and_1_out, and_2_out, not_1_out;

  and and_1 (and_1_out, _0, not_1_out);
  not not_1 (not_1_out, S);
  and and_2 (and_2_out, _1, S);
  or or_1 (U, and_1_out, and_2_out);
endmodule

module Add_8 (
  input  A0,
  input  A1,
  input  A2,
  input  A3,
  input  A4,
  input  A5,
  input  A6,
  input  AN,
  input  B0,
  input  B1,
  input  B2,
  input  B3,
  input  B4,
  input  B5,
  input  B6,
  input  BN,
  output S0,
  output S1,
  output S2,
  output S3,
  output S4,
  output S5,
  output S6,
  output SN,
  output SO
);

  wire fulladder_1_u, fulladder_2_u, fulladder_3_u, fulladder_4_u, fulladder_5_u, fulladder_6_u,
       semiadder_1_u;

  semiadder semiadder_1 (.A(A0), .B(B0), .U(semiadder_1_u), .S(S0));
  fulladder fulladder_1 (.A(A1), .B(B1), .D(semiadder_1_u), .U(fulladder_1_u), .S(S1));
  fulladder fulladder_2 (.A(A2), .B(B2), .D(fulladder_1_u), .U(fulladder_2_u), .S(S2));
  fulladder fulladder_3 (.A(A3), .B(B3), .D(fulladder_2_u), .U(fulladder_3_u), .S(S3));
  fulladder fulladder_4 (.A(A4), .B(B4), .D(fulladder_3_u), .U(fulladder_4_u), .S(S4));
  fulladder fulladder_5 (.A(A5), .B(B5), .D(fulladder_4_u), .U(fulladder_5_u), .S(S5));
  fulladder fulladder_6 (.A(A6), .B(B6), .D(fulladder_5_u), .U(fulladder_6_u), .S(S6));
  fulladder fulladder_7 (.A(AN), .B(BN), .D(fulladder_6_u), .U(SO), .S(SN));
endmodule

module PU (
  input  in_1,
  input  in_2,
  input  in_3,
  input  in_4,
  input  in_5,
  input  in_6,
  input  in_7,
  input  in_8,
  input  in_9,
  input  in_10,
  input  in_11,
  input  in_12,
  input  in_13,
  input  in_14,
  input  in_15,
  input  in_16,
  input  in_17,
  input  in_18,
  input  in_19,
  input  in_20,
  output out_21
);
endmodule

module AddSub (
  input  A0,
  input  A1,
  input  A2,
  input  A3,
  input  A4,
  input  A5,
  input  A6,
  input  AN,
  input  RUN,
  input  CLK,
  input  SUB,
  input  B0,
  input  B1,
  input  B2,
  input  B3,
  input  B4,
  input  B5,
  input  B6,
  input  BN,
  output S0,
  output S1,
  output S2,
  output S3,
  output S4,
  output S5,
  output S6,
  output SN,
  output SU
);

  wire and_1_out, and_2_out, sel_8_1_s0, sel_8_1_s1, sel_8_1_s2, sel_8_1_s3, sel_8_1_s4, sel_8_1_s5,
       sel_8_1_s6, sel_8_1_sn, sub_1_s0, sub_1_s1, sub_1_s2, sub_1_s3, sub_1_s4, sub_1_s5, sub_1_s6,
       sub_1_sn, sw_8_1_s0, sw_8_1_s1, sw_8_1_s2, sw_8_1_s3, sw_8_1_s4, sw_8_1_s5, sw_8_1_s6, sw_8_1_sn,
       sw_8_2_s0, sw_8_2_s1, sw_8_2_s2, sw_8_2_s3, sw_8_2_s4, sw_8_2_s5, sw_8_2_s6, sw_8_2_sn;

  and and_1 (and_1_out, RUN, CLK);
  and and_2 (and_2_out, and_1_out, SUB);
  SW_8 sw_8_1 (
    .A0(B0), .A1(B1), .A2(B2), .A3(B3), .A4(B4), .A5(B5), .A6(B6), .AN(BN), .S(and_1_out), .S0(sw_8_1_s0),
    .S1(sw_8_1_s1), .S2(sw_8_1_s2), .S3(sw_8_1_s3), .S4(sw_8_1_s4), .S5(sw_8_1_s5), .S6(sw_8_1_s6),
    .SN(sw_8_1_sn));
  SW_8 sw_8_2 (
    .A0(AN), .A1(A6), .A2(A5), .A3(A4), .A4(A3), .A5(A2), .A6(A1), .AN(A0), .S(and_1_out), .S0(sw_8_2_s0),
    .S1(sw_8_2_s1), .S2(sw_8_2_s2), .S3(sw_8_2_s3), .S4(sw_8_2_s4), .S5(sw_8_2_s5), .S6(sw_8_2_s6),
    .SN(sw_8_2_sn));
  Sub sub_1 (
    .A0(sw_8_1_s0), .A1(sw_8_1_s1), .A2(sw_8_1_s2), .A3(sw_8_1_s3), .A4(sw_8_1_s4), .A5(sw_8_1_s5),
    .A6(sw_8_1_s6), .AN(sw_8_1_sn), .S0(sub_1_s0), .S1(sub_1_s1), .S2(sub_1_s2), .S3(sub_1_s3),
    .S4(sub_1_s4), .S5(sub_1_s5), .S6(sub_1_s6), .SN(sub_1_sn));  // open: SO
  Sel_8 sel_8_1 (
    .A0(sw_8_1_s0), .A1(sw_8_1_s1), .A2(sw_8_1_s2), .A3(sw_8_1_s3), .A4(sw_8_1_s4), .A5(sw_8_1_s5),
    .A6(sw_8_1_s6), .AN(sw_8_1_sn), .B0(sub_1_s0), .B1(sub_1_s1), .B2(sub_1_s2), .B3(sub_1_s3),
    .B4(sub_1_s4), .B5(sub_1_s5), .B6(sub_1_s6), .BN(sub_1_sn), .S(and_2_out), .S0(sel_8_1_s0),
    .S1(sel_8_1_s1), .S2(sel_8_1_s2), .S3(sel_8_1_s3), .S4(sel_8_1_s4), .S5(sel_8_1_s5), .S6(sel_8_1_s6),
    .SN(sel_8_1_sn));
  Add_8 add_8_1 (
    .A0(sw_8_2_sn), .A1(sw_8_2_s6), .A2(sw_8_2_s5), .A3(sw_8_2_s4), .A4(sw_8_2_s3), .A5(sw_8_2_s2),
    .A6(sw_8_2_s1), .AN(sw_8_2_s0), .B0(sel_8_1_s0), .B1(sel_8_1_s1), .B2(sel_8_1_s2), .B3(sel_8_1_s3),
    .B4(sel_8_1_s4), .B5(sel_8_1_s5), .B6(sel_8_1_s6), .BN(sel_8_1_sn), .S0(S0), .S1(S1), .S2(S2), .S3(S3),
    .S4(S4), .S5(S5), .S6(S6), .SN(SN), .SO(SU));
endmodule

module Sub (
  input  A0,
  input  A1,
  input  A2,
  input  A3,
  input  A4,
  input  A5,
  input  A6,
  input  AN,
  output S0,
  output S1,
  output S2,
  output S3,
  output S4,
  output S5,
  output S6,
  output SN,
  output SO
);

  wire not_1_out, not_2_out, not_3_out, not_4_out, not_5_out, not_6_out, not_7_out;

  not not_1 (not_1_out, A0);
  not not_2 (not_2_out, A1);
  not not_3 (not_3_out, A2);
  not not_4 (not_4_out, A3);
  not not_5 (not_5_out, A4);
  not not_6 (not_6_out, A5);
  not not_7 (not_7_out, A6);
  not not_8 (SN, AN);
  Add_8 add_8_1 (
    .A0(not_1_out), .A1(not_2_out), .A2(not_3_out), .A3(not_4_out), .A4(not_5_out), .A5(not_6_out),
    .A6(not_7_out), .AN(1'b0), .B0(1'b1), .B1(1'b0), .B2(1'b0), .B3(1'b0), .B4(1'b0), .B5(1'b0), .B6(1'b0),
    .BN(1'b0), .S0(S0), .S1(S1), .S2(S2), .S3(S3), .S4(S4), .S5(S5), .S6(S6), .SO(SO));  // open: SN
endmodule

module Div_2 (
  input  S,
  input  _0,
  output U0,
  output U1
);

  wire not_1_out;

  not not_1 (not_1_out, S);
  and and_1 (U0, not_1_out, _0);
  and and_2 (U1, _0, S);
endmodule

module Merger_8 (
  input  A0,
  input  A1,
  input  A2,
  input  A3,
  input  A4,
  input  A5,
  input  A6,
  input  AN,
  input  B0,
  input  B1,
  input  B2,
  input  B3,
  input  B4,
  input  B5,
  input  B6,
  input  BN,
  output S0,
  output S1,
  output S2,
  output S3,
  output S4,
  output S5,
  output S6,
  output SN
);

  or or_1 (S0, A0, B0);
  or or_2 (S1, A1, B1);
  or or_3 (S2, A2, B2);
  or or_4 (S3, A3, B3);
  or or_5 (S4, A4, B4);
  or or_6 (S5, A5, B5);
  or or_7 (S6, A6, B6);
  or or_8 (SN, AN, BN);
endmodule

module Sel_8 (
  input  A0,
  input  A1,
  input  A2,
  input  A3,
  input  A4,
  input  A5,
  input  A6,
  input  AN,
  input  B0,
  input  B1,
  input  B2,
  input  B3,
  input  B4,
  input  B5,
  input  S,
  input  B6,
  input  BN,
  output S0,
  output S1,
  output S2,
  output S3,
  output S4,
  output S5,
  output S6,
  output SN
);

  Sel_2 sel_2_1 (._0(A0), ._1(B0), .S(S), .U(S0));
  Sel_2 sel_2_2 (._0(A1), ._1(B1), .S(S), .U(S1));
  Sel_2 sel_2_3 (._0(A2), ._1(B2), .S(S), .U(S2));
  Sel_2 sel_2_4 (._0(A3), ._1(B3), .S(S), .U(S3));
  Sel_2 sel_2_5 (._0(A4), ._1(B4), .S(S), .U(S4));
  Sel_2 sel_2_6 (._0(A5), ._1(B5), .S(S), .U(S5));
  Sel_2 sel_2_7 (._0(A6), ._1(B6), .S(S), .U(S6));
  Sel_2 sel_2_8 (._0(AN), ._1(BN), .S(S), .U(SN));
endmodule

module SW_8 (
  input  A0,
  input  A1,
  input  A2,
  input  A3,
  input  A4,
  input  A5,
  input  S,
  input  A6,
  input  AN,
  output S0,
  output S1,
  output S2,
  output S3,
  output S4,
  output S5,
  output S6,
  output SN
);

  Sel_8 sel_8_1 (
    .A0(1'b0), .A1(1'b0), .A2(1'b0), .A3(1'b0), .A4(1'b0), .A5(1'b0), .A6(1'b0), .AN(1'b0), .B0(A0), .B1(A1),
    .B2(A2), .B3(A3), .B4(A4), .B5(A5), .B6(A6), .BN(AN), .S(S), .S0(S0), .S1(S1), .S2(S2), .S3(S3), .S4(S4),
    .S5(S5), .S6(S6), .SN(SN));
endmodule
